// Logisim project 32-Bit-Register.circ as structural Verilog: 1 circuit, main circuit main
module main (
  input  in_1,
  input  in_2,
  input  in_3,
  input  in_4,
  input  in_5,
  input  in_6,
  input  in_7,
  input  in_8,
  input  in_9,
  input  in_10,
  input  in_11,
  input  in_12,
  output out_13,
  output out_14,
  output out_15,
  output out_16,
  output out_17,
  output out_18,
  output out_19,
  output out_20
);

  wire and_1_out, and_2_out, and_3_out, and_4_out, and_5_out, and_6_out, and_7_out, and_8_out, and_9_out,
       and_10_out, and_11_out, and_12_out, and_13_out, and_14_out, and_15_out, and_16_out, and_17_out,
       and_18_out, and_19_out, and_20_out, and_21_out, and_22_out, and_23_out, and_24_out, and_25_out,
       and_26_out, and_27_out, and_28_out, and_29_out, and_30_out, and_31_out, and_32_out, and_33_out,
       and_34_out, and_35_out, and_36_out, and_37_out, and_38_out, and_39_out, and_40_out, d_ff_1_q,
       d_ff_2_q, d_ff_3_q, d_ff_4_q, d_ff_5_q, d_ff_6_q, d_ff_7_q, d_ff_8_q, d_ff_9_q, d_ff_10_q, d_ff_11_q,
       d_ff_12_q, d_ff_13_q, d_ff_14_q, d_ff_15_q, d_ff_16_q, d_ff_17_q, d_ff_18_q, d_ff_19_q, d_ff_20_q,
       d_ff_21_q, d_ff_22_q, d_ff_23_q, d_ff_24_q, d_ff_25_q, d_ff_26_q, d_ff_27_q, d_ff_28_q, d_ff_29_q,
       d_ff_30_q, d_ff_31_q, d_ff_32_q, not_1_out, not_2_out, not_3_out, not_4_out;

  and and_1 (and_1_out, and_11_out, d_ff_4_q);
  and and_2 (and_2_out, and_11_out, d_ff_12_q);
  and and_3 (and_3_out, and_11_out, d_ff_8_q);
  and and_4 (and_4_out, and_11_out, d_ff_20_q);
  and and_5 (and_5_out, and_11_out, d_ff_16_q);
  not not_1 (not_1_out, in_10);
  not not_2 (not_2_out, in_1);
  not not_3 (not_3_out, in_10);
  not not_4 (not_4_out, in_1);
  and and_6 (and_6_out, and_11_out, d_ff_24_q);
  and and_7 (and_7_out, and_11_out, d_ff_28_q);
  and and_8 (and_8_out, not_1_out, not_2_out);
  and and_9 (and_9_out, not_3_out, in_1);
  and and_10 (and_10_out, in_10, not_4_out);
  and and_11 (and_11_out, in_1, in_10);
  and and_12 (and_12_out, in_12, and_11_out);
  and and_13 (and_13_out, and_10_out, d_ff_3_q);
  and and_14 (and_14_out, and_11_out, d_ff_32_q);
  and and_15 (and_15_out, in_12, and_10_out);
  and and_16 (and_16_out, in_12, and_9_out);
  D_Flip_Flop d_ff_1 (.clk(and_19_out), .D(in_2), .Q(d_ff_1_q), .reset(in_11));  // open: Qn, preset, en
  D_Flip_Flop d_ff_2 (.clk(and_16_out), .D(in_2), .Q(d_ff_2_q), .reset(in_11));  // open: Qn, preset, en
  D_Flip_Flop d_ff_3 (.clk(and_15_out), .D(in_2), .Q(d_ff_3_q), .reset(in_11));  // open: Qn, preset, en
  D_Flip_Flop d_ff_4 (.clk(and_12_out), .D(in_2), .Q(d_ff_4_q), .reset(in_11));  // open: Qn, preset, en
  and and_17 (and_17_out, and_10_out, d_ff_7_q);
  and and_18 (and_18_out, and_10_out, d_ff_11_q);
  and and_19 (and_19_out, in_12, and_8_out);
  and and_20 (and_20_out, and_10_out, d_ff_15_q);
  and and_21 (and_21_out, and_10_out, d_ff_19_q);
  D_Flip_Flop d_ff_5 (.clk(and_19_out), .D(in_3), .Q(d_ff_5_q), .reset(in_11));  // open: Qn, preset, en
  D_Flip_Flop d_ff_6 (.clk(and_16_out), .D(in_3), .Q(d_ff_6_q), .reset(in_11));  // open: Qn, preset, en
  D_Flip_Flop d_ff_7 (.clk(and_15_out), .D(in_3), .Q(d_ff_7_q), .reset(in_11));  // open: Qn, preset, en
  D_Flip_Flop d_ff_8 (.clk(and_12_out), .D(in_3), .Q(d_ff_8_q), .reset(in_11));  // open: Qn, preset, en
  and and_22 (and_22_out, and_10_out, d_ff_23_q);
  and and_23 (and_23_out, and_10_out, d_ff_27_q);
  or or_1 (out_17, and_4_out, and_21_out, and_29_out, and_38_out);
  or or_2 (out_13, and_1_out, and_13_out, and_25_out, and_33_out);
  D_Flip_Flop d_ff_9 (.clk(and_19_out), .D(in_4), .Q(d_ff_9_q), .reset(in_11));  // open: Qn, preset, en
  D_Flip_Flop d_ff_10 (.clk(and_16_out), .D(in_4), .Q(d_ff_10_q), .reset(in_11));  // open: Qn, preset, en
  D_Flip_Flop d_ff_11 (.clk(and_15_out), .D(in_4), .Q(d_ff_11_q), .reset(in_11));  // open: Qn, preset, en
  D_Flip_Flop d_ff_12 (.clk(and_12_out), .D(in_4), .Q(d_ff_12_q), .reset(in_11));  // open: Qn, preset, en
  and and_24 (and_24_out, and_10_out, d_ff_31_q);
  and and_25 (and_25_out, and_9_out, d_ff_2_q);
  or or_3 (out_18, and_6_out, and_22_out, and_31_out, and_37_out);
  or or_4 (out_14, and_3_out, and_17_out, and_27_out, and_34_out);
  D_Flip_Flop d_ff_13 (.clk(and_19_out), .D(in_5), .Q(d_ff_13_q), .reset(in_11));  // open: Qn, preset, en
  D_Flip_Flop d_ff_14 (.clk(and_16_out), .D(in_5), .Q(d_ff_14_q), .reset(in_11));  // open: Qn, preset, en
  D_Flip_Flop d_ff_15 (.clk(and_15_out), .D(in_5), .Q(d_ff_15_q), .reset(in_11));  // open: Qn, preset, en
  D_Flip_Flop d_ff_16 (.clk(and_12_out), .D(in_5), .Q(d_ff_16_q), .reset(in_11));  // open: Qn, preset, en
  and and_26 (and_26_out, and_9_out, d_ff_10_q);
  and and_27 (and_27_out, and_9_out, d_ff_6_q);
  or or_5 (out_19, and_7_out, and_23_out, and_30_out, and_40_out);
  or or_6 (out_15, and_2_out, and_18_out, and_26_out, and_36_out);
  D_Flip_Flop d_ff_17 (.clk(and_19_out), .D(in_6), .Q(d_ff_17_q), .reset(in_11));  // open: Qn, preset, en
  D_Flip_Flop d_ff_18 (.clk(and_16_out), .D(in_6), .Q(d_ff_18_q), .reset(in_11));  // open: Qn, preset, en
  D_Flip_Flop d_ff_19 (.clk(and_15_out), .D(in_6), .Q(d_ff_19_q), .reset(in_11));  // open: Qn, preset, en
  D_Flip_Flop d_ff_20 (.clk(and_12_out), .D(in_6), .Q(d_ff_20_q), .reset(in_11));  // open: Qn, preset, en
  and and_28 (and_28_out, and_9_out, d_ff_14_q);
  and and_29 (and_29_out, and_9_out, d_ff_18_q);
  or or_7 (out_20, and_14_out, and_24_out, and_32_out, and_39_out);
  or or_8 (out_16, and_5_out, and_20_out, and_28_out, and_35_out);
  and and_30 (and_30_out, and_9_out, d_ff_26_q);
  and and_31 (and_31_out, and_9_out, d_ff_22_q);
  D_Flip_Flop d_ff_21 (.clk(and_19_out), .D(in_7), .Q(d_ff_21_q), .reset(in_11));  // open: Qn, preset, en
  D_Flip_Flop d_ff_22 (.clk(and_16_out), .D(in_7), .Q(d_ff_22_q), .reset(in_11));  // open: Qn, preset, en
  D_Flip_Flop d_ff_23 (.clk(and_15_out), .D(in_7), .Q(d_ff_23_q), .reset(in_11));  // open: Qn, preset, en
  D_Flip_Flop d_ff_24 (.clk(and_12_out), .D(in_7), .Q(d_ff_24_q), .reset(in_11));  // open: Qn, preset, en
  and and_32 (and_32_out, and_9_out, d_ff_30_q);
  D_Flip_Flop d_ff_25 (.clk(and_19_out), .D(in_8), .Q(d_ff_25_q), .reset(in_11));  // open: Qn, preset, en
  D_Flip_Flop d_ff_26 (.clk(and_16_out), .D(in_8), .Q(d_ff_26_q), .reset(in_11));  // open: Qn, preset, en
  D_Flip_Flop d_ff_27 (.clk(and_15_out), .D(in_8), .Q(d_ff_27_q), .reset(in_11));  // open: Qn, preset, en
  D_Flip_Flop d_ff_28 (.clk(and_12_out), .D(in_8), .Q(d_ff_28_q), .reset(in_11));  // open: Qn, preset, en
  and and_33 (and_33_out, and_8_out, d_ff_1_q);
  and and_34 (and_34_out, and_8_out, d_ff_5_q);
  D_Flip_Flop d_ff_29 (.clk(and_19_out), .D(in_9), .Q(d_ff_29_q), .reset(in_11));  // open: Qn, preset, en
  D_Flip_Flop d_ff_30 (.clk(and_16_out), .D(in_9), .Q(d_ff_30_q), .reset(in_11));  // open: Qn, preset, en
  D_Flip_Flop d_ff_31 (.clk(and_15_out), .D(in_9), .Q(d_ff_31_q), .reset(in_11));  // open: Qn, preset, en
  D_Flip_Flop d_ff_32 (.clk(and_12_out), .D(in_9), .Q(d_ff_32_q), .reset(in_11));  // open: Qn, preset, en
  and and_35 (and_35_out, and_8_out, d_ff_13_q);
  and and_36 (and_36_out, and_8_out, d_ff_9_q);
  and and_37 (and_37_out, and_8_out, d_ff_21_q);
  and and_38 (and_38_out, and_8_out, d_ff_17_q);
  and and_39 (and_39_out, and_8_out, d_ff_29_q);
  and and_40 (and_40_out, and_8_out, d_ff_25_q);
endmodule
