// Logisim project 8-Bit-Register.circ as structural Verilog: 1 circuit, main circuit main
module main (
  input  in_1,
  input  in_2,
  input  Write,
  input  Read,
  input  in_5,
  input  in_6,
  input  Inputs,
  input  in_8,
  input  Clear,
  output out_10,
  output out_11,
  output out_12,
  output out_13
);

  wire and_5_out, and_6_out, and_7_out, and_8_out, and_9_out, and_10_out, and_11_out, and_12_out, and_13_out,
       and_14_out, and_15_out, and_16_out, and_17_out, and_18_out, and_19_out, and_20_out, and_21_out,
       and_22_out, and_23_out, and_24_out, and_25_out, and_26_out, and_27_out, and_28_out, d_ff_1_q,
       d_ff_2_q, d_ff_3_q, d_ff_4_q, d_ff_5_q, d_ff_6_q, d_ff_7_q, d_ff_8_q, d_ff_9_q, d_ff_10_q, d_ff_11_q,
       d_ff_12_q, d_ff_13_q, d_ff_14_q, d_ff_15_q, d_ff_16_q, not_1_out, not_2_out, not_3_out, not_4_out,
       or_1_out, or_2_out, or_3_out, or_4_out;

  and and_1 (out_10, Read, or_4_out);
  and and_2 (out_11, Read, or_3_out);
  and and_3 (out_12, Read, or_2_out);
  and and_4 (out_13, Read, or_1_out);
  not not_1 (not_1_out, in_1);
  not not_2 (not_2_out, in_2);
  not not_3 (not_3_out, in_1);
  not not_4 (not_4_out, in_2);
  and and_5 (and_5_out, not_1_out, not_2_out);
  and and_6 (and_6_out, not_3_out, in_2);
  and and_7 (and_7_out, in_1, not_4_out, not_4_out);
  and and_8 (and_8_out, in_1, in_2);
  D_Flip_Flop d_ff_1 (.clk(and_9_out), .D(in_8), .Q(d_ff_1_q), .reset(Clear));  // open: Qn, preset, en
  D_Flip_Flop d_ff_2 (.clk(and_10_out), .D(in_8), .Q(d_ff_2_q), .reset(Clear));  // open: Qn, preset, en
  and and_9 (and_9_out, Write, and_8_out);
  D_Flip_Flop d_ff_3 (.clk(and_9_out), .D(Inputs), .Q(d_ff_3_q), .reset(Clear));  // open: Qn, preset, en
  D_Flip_Flop d_ff_4 (.clk(and_10_out), .D(Inputs), .Q(d_ff_4_q), .reset(Clear));  // open: Qn, preset, en
  D_Flip_Flop d_ff_5 (.clk(and_9_out), .D(in_6), .Q(d_ff_5_q), .reset(Clear));  // open: Qn, preset, en
  D_Flip_Flop d_ff_6 (.clk(and_10_out), .D(in_6), .Q(d_ff_6_q), .reset(Clear));  // open: Qn, preset, en
  and and_10 (and_10_out, Write, and_7_out);
  D_Flip_Flop d_ff_7 (.clk(and_9_out), .D(in_5), .Q(d_ff_7_q), .reset(Clear));  // open: Qn, preset, en
  D_Flip_Flop d_ff_8 (.clk(and_10_out), .D(in_5), .Q(d_ff_8_q), .reset(Clear));  // open: Qn, preset, en
  and and_11 (and_11_out, Write, and_6_out);
  and and_12 (and_12_out, Write, and_5_out);
  D_Flip_Flop d_ff_9 (.clk(and_12_out), .D(in_8), .Q(d_ff_9_q), .reset(Clear));  // open: Qn, preset, en
  D_Flip_Flop d_ff_10 (.clk(and_11_out), .D(in_8), .Q(d_ff_10_q), .reset(Clear));  // open: Qn, preset, en
  D_Flip_Flop d_ff_11 (.clk(and_12_out), .D(Inputs), .Q(d_ff_11_q), .reset(Clear));  // open: Qn, preset, en
  D_Flip_Flop d_ff_12 (.clk(and_11_out), .D(Inputs), .Q(d_ff_12_q), .reset(Clear));  // open: Qn, preset, en
  D_Flip_Flop d_ff_13 (.clk(and_12_out), .D(in_6), .Q(d_ff_13_q), .reset(Clear));  // open: Qn, preset, en
  D_Flip_Flop d_ff_14 (.clk(and_11_out), .D(in_6), .Q(d_ff_14_q), .reset(Clear));  // open: Qn, preset, en
  D_Flip_Flop d_ff_15 (.clk(and_12_out), .D(in_5), .Q(d_ff_15_q), .reset(Clear));  // open: Qn, preset, en
  D_Flip_Flop d_ff_16 (.clk(and_11_out), .D(in_5), .Q(d_ff_16_q), .reset(Clear));  // open: Qn, preset, en
  and and_13 (and_13_out, and_5_out, d_ff_9_q);
  and and_14 (and_14_out, and_5_out, d_ff_11_q);
  and and_15 (and_15_out, and_5_out, d_ff_13_q);
  and and_16 (and_16_out, and_5_out, d_ff_15_q);
  and and_17 (and_17_out, and_6_out, d_ff_10_q);
  and and_18 (and_18_out, and_6_out, d_ff_12_q);
  and and_19 (and_19_out, and_6_out, d_ff_14_q);
  and and_20 (and_20_out, and_6_out, d_ff_16_q);
  and and_21 (and_21_out, and_7_out, d_ff_2_q);
  and and_22 (and_22_out, and_7_out, d_ff_4_q);
  and and_23 (and_23_out, and_7_out, d_ff_6_q);
  and and_24 (and_24_out, and_7_out, d_ff_8_q);
  and and_25 (and_25_out, and_8_out, d_ff_1_q);
  and and_26 (and_26_out, and_8_out, d_ff_3_q);
  and and_27 (and_27_out, and_8_out, d_ff_5_q);
  and and_28 (and_28_out, and_8_out, d_ff_7_q);
  or or_1 (or_1_out, and_21_out, and_13_out, and_25_out, and_17_out);
  or or_2 (or_2_out, and_14_out, and_22_out, and_18_out, and_26_out);
  or or_3 (or_3_out, and_15_out, and_23_out, and_19_out, and_27_out);
  or or_4 (or_4_out, and_16_out, and_24_out, and_20_out, and_28_out);

  // Notes on the sheet:
  //   Outputs
  //   Select
  //   16-Bit-Register
endmodule
